# Fritzing sketch relogio (saved by Fritzing 0.9.6b)
breadboards: 1

parts:
  Componente1 = Arduino Pro Mini (5V)
  IC1 = DS1307 [package=THT]  # not connected
  Componente2 = Real Time Clock Module - DS1307 RTC Breakout Board
  Q1 = NPN-Transistor [package="TO92 [THT]"]
  IR1 = TSOP312.., 314.. [package=THT]
  RFM12b1 = RFM12b HopeRF Transceiver  # not connected
  J1 = Piezo Speaker
  S1 = Pushbutton [package="[THT]"]
  S2 = Pushbutton [package="[THT]"]
  S3 = Pushbutton [package="[THT]"]
  LED1 = LED - 3mm [color="Red (633nm)" current=30mA package="3 mm [THT]"]
  Grove1 = Grove OLED 128x96
  R1 = Resistor [tolerance=±5% resistance=220 package="0603 [SMD]"]
  R2 = Resistor [tolerance=±5% resistance=220 package="0603 [SMD]"]
  R3 = Resistor [tolerance=±5% resistance=220 package="0603 [SMD]"]
  BAT1 = LIPO-110mAh [package=lipo-110]  # not connected
  BAT1_2 = Battery Holders [package=lipo-1100mAh]  # not connected
  BAT1_3 = Battery Holders [package=lipo-1100mAh]  # not connected
  BAT1_4 = Battery Holders [package=lipo-1100mAh]

nets:
  N1: Componente1.A4, Componente2.SDA, Grove1.SDA
  N2: Componente1.A5, Componente2.SCL, Grove1.SCL
  N3: Componente1.SCK, J1.pin2
  N4: Componente1.D8, IR1.Data
  N5: Componente1.D6, Q1.B
  5V: Componente2.5V, IR1.Vs, S1.Pin_1, S2.Pin_1, S2.Pin_2, S3.Pin_1, S3.Pin_2, LED1.anode, Grove1.VCC, BAT1_4.+
  GND: Componente2.GND, Q1.C, IR1.GND, J1.pin1, Grove1.GND, R1.Pin_1, R2.Pin_1, R3.Pin_1, BAT1_4.-
  N6: Q1.E, LED1.cathode
